// Logisim project Guia_0501.circ as structural Verilog: 1 circuit, main circuit main
// not_a
module main (
  input  a,
  input  b,
  output s
);

  wire NOR1_out, nor_1_out, nor_2_out;

  nor nor_1 (nor_1_out, NOR1_out, NOR1_out);
  nor NOR1 (NOR1_out, a, a);
  nor nor_2 (nor_2_out, b, b);
  nor nor_3 (s, nor_1_out, nor_2_out);
endmodule
