// Logisim project Guia_0505.circ as structural Verilog: 1 circuit, main circuit main
module main (
  input  a,
  input  b,
  output s
);

  wire xor_1_out, xor_2_out, xor_3_out, xor_4_out, xor_6_out;

  xor xor_1 (xor_1_out, a, a);
  xor xor_2 (xor_2_out, a, xor_1_out);
  xor xor_3 (xor_3_out, xor_1_out, a);
  xor xor_4 (xor_4_out, xor_2_out, xor_3_out);
  xor xor_5 (s, xor_6_out, xor_6_out);
  xor xor_6 (xor_6_out, xor_4_out, xor_4_out);
endmodule
