// Logisim project Guia_0608.circ as structural Verilog: 1 circuit, main circuit main
module main (
  input  a,
  input  b,
  input  c,
  input  d,
  output s
);

  wire and_1_out, and_2_out, and_3_out, and_4_out, not_1_out, not_2_out, not_3_out, not_4_out, not_5_out,
       not_6_out;

  not not_1 (not_1_out, b);
  not not_2 (not_2_out, a);
  not not_3 (not_3_out, b);
  not not_4 (not_4_out, c);
  not not_5 (not_5_out, a);
  not not_6 (not_6_out, d);
  and and_1 (and_1_out, c, a, b, d);
  and and_2 (and_2_out, c, a, not_1_out, d);
  and and_3 (and_3_out, c, not_2_out, not_3_out, d);
  and and_4 (and_4_out, not_4_out, not_5_out, b, not_6_out);
  or or_1 (s, and_1_out, and_2_out, and_3_out, and_4_out);

  // Notes on the sheet:
  //   Caio Faria Diniz - 793605
  //   Guia_608 extra
  //   Expressão: f(w,x,y,z) = (w.x.y.z) + (w.x.y'.z') + (w.x'.y'.z) + (w'.x'.y.z')
endmodule
