// Logisim project Guia_0702.circ as structural Verilog: 1 circuit, main circuit main
module main (
  input  x,
  input  y,
  input  s,
  output z
);

  wire NOR_out, OR_out;

  nor NOR (NOR_out, x, y);
  or OR (OR_out, x, y);
  // MUX_2x1 mux_2x1_1: pin names not known; wires that end beside it: x, y, NOR_out, NOR_out, OR_out, s, z

  // Notes on the sheet:
  //   Guia_0702
  //   Caio Faria Diniz - 793605
endmodule
