// Logisim project Guia_0703.circ as structural Verilog: 1 circuit, main circuit main
module main (
  input  x,
  input  y,
  input  s1,
  input  S3,
  input  s2,
  output z
);

  wire AND_out, mux_2x1_1_p4, mux_2x1_2_p8, NAND_out, NOR_out, OR_out;

  and AND (AND_out, x, y);
  or OR (OR_out, x, y);
  nand NAND (NAND_out, x, y);
  nor NOR (NOR_out, x, y);
  // MUX_2x1 mux_2x1_1: pin names not known; wires that end beside it: AND_out, OR_out, s1, mux_2x1_1_p4
  // MUX_2x1 mux_2x1_2: pin names not known; wires that end beside it: x, y, NAND_out, NOR_out, NAND_out, NOR_out, s2, mux_2x1_2_p8
  // MUX_2x1 mux_2x1_3: pin names not known; wires that end beside it: mux_2x1_1_p4, mux_2x1_2_p8, S3, z

  // Notes on the sheet:
  //   Guia_0703
  //   Caio Faria Diniz - 793605
endmodule
