// Logisim project Guia_0705.circ as structural Verilog: 1 circuit, main circuit main
module main (
  input  x,
  input  y,
  input  in_3,
  input  in_4,
  input  in_5,
  output z
);

  wire AND_out, NAND_out, NOR_out, NOT_X_out, NOT_Y_out, OR_out, XNOR_out, XOR_out;

  not NOT_X (NOT_X_out, x);
  not NOT_Y (NOT_Y_out, y);
  and AND (AND_out, x, y);
  nand NAND (NAND_out, x, y);
  or OR (OR_out, x, y);
  nor NOR (NOR_out, x, y);
  xor XOR (XOR_out, x, y);
  xnor XNOR (XNOR_out, x, y);
  // MUX_8x3 mux_8x3_1: pin names not known; wires that end beside it: NOT_X_out, NOT_Y_out, AND_out, NAND_out, OR_out, NOR_out, XOR_out, XNOR_out, in_3, in_4, in_5, z

  // Notes on the sheet:
  //   Guia_0705
  //   Caio Faria Diniz - 793605
endmodule
