// Logisim project Guia_0805.circ as structural Verilog: 2 circuits, main circuit main
module main (
  input  x5,
  input  x4,
  input  x3,
  input  x2,
  input  x1,
  input  x0,
  output s5,
  output s4,
  output s3,
  output s2,
  output s1,
  output s0,
  output carryOut
);

  wire c1_1_out_10, c1_1_out_11, c1_1_out_12, fa_1_p2, fa_1_p4, fa_2_p2, fa_2_p3, fa_2_p4, fa_3_p1, fa_4_p4,
       fa_5_p4;

  // FA fa_1: pin names not known; wires that end beside it: 1'b0, fa_1_p2, carryOut, fa_1_p4, s5
  // FA fa_2: pin names not known; wires that end beside it: 1'b0, fa_2_p2, fa_2_p3, fa_2_p4, s3
  // FA fa_3: pin names not known; wires that end beside it: fa_3_p1, fa_1_p4, fa_2_p3, s4
  C1 c1_1 (
    .in_1(x5), .in_2(x4), .in_3(x3), .in_4(x2), .in_5(x1), .in_6(x0), .out_7(fa_1_p2), .out_8(fa_3_p1),
    .out_9(fa_2_p2), .out_10(c1_1_out_10), .out_11(c1_1_out_11), .out_12(c1_1_out_12));
  // FA fa_4: pin names not known; wires that end beside it: 1'b0, c1_1_out_10, fa_2_p4, fa_4_p4, s2
  // FA fa_5: pin names not known; wires that end beside it: 1'b0, c1_1_out_11, fa_4_p4, fa_5_p4, s1
  // FA fa_6: pin names not known; wires that end beside it: 1'b1, c1_1_out_12, fa_5_p4, 1'b0, s0

  // Notes on the sheet:
  //   Caio Faria Diniz - 793605$Guia_0805$Two's Complement for 6 bits
  //   carryIn
endmodule

module C1 (
  input  in_1,
  input  in_2,
  input  in_3,
  input  in_4,
  input  in_5,
  input  in_6,
  output out_7,
  output out_8,
  output out_9,
  output out_10,
  output out_11,
  output out_12
);

  not not_1 (out_7, in_1);
  not not_2 (out_8, in_2);
  not not_3 (out_9, in_3);
  not not_4 (out_11, in_5);
  not not_5 (out_10, in_4);
  not not_6 (out_12, in_6);

  // Notes on the sheet:
  //   One's complement for 6 bits
endmodule
